# Fritzing sketch BLE Arduino Encoder with LEDs (saved by Fritzing 0.9.1b)
breadboards: 1

parts:
  Arduino = Blend Micro v1.0
  CHARGER1 = USB_LiIon_LiPoly_Charger_v1.2
  BATT1 = LiPoly Battery (1300mAh)
  U1 = ENCODER_2LED [package=encoder_led_2]
  R1 = Resistor [tolerance=±5% resistance=100 package=THT]
  R2 = Resistor [tolerance=±5% resistance=100 package=THT]
  R3 = Resistor [tolerance=±5% resistance=10k package=THT]
  R4 = Resistor [tolerance=±5% resistance=10k package=THT]
  Q1 = PNP-Transistor [package="TO92 [THT]"]
  Q2 = NPN-Transistor [package="TO92 [THT]"]
  R5 = Resistor [tolerance=±5% resistance=100k package=THT]
  R6 = Resistor [tolerance=±5% resistance=10k package=THT]
  R7 = Resistor [tolerance=±5% resistance=100k package=THT]
  Q3 = NPN-Transistor [package="TO92 [THT]"]
  R8 = Resistor [tolerance=±5% resistance=4.7k package=THT]
  D1 = Rectifier Diode [part_number=1N4001 package="300 mil [THT]"]
  D2 = Rectifier Diode [part_number=1N4001 package="300 mil [THT]"]

nets (from the schematic view):
  N1: Arduino.D5/PWM, R8.Pin_0
  N2: Arduino.D3/SCL/PWM, D1.anode
  N3: Arduino.D2/SDA, U1.B
  N4: Arduino.D1/TX, U1.C
  N5: Arduino.D0/RX, U1.A
  N6: Arduino.VIN, R4.Pin_0, Q1.E
  N7: Arduino.GND#13, Arduino.GND#35, CHARGER1.dcin_minus_1, U1.-, R3.Pin_1, Q2.E, Q3.E
  N8: Arduino.D9/PWM/A9, R1.Pin_0
  N9: Arduino.D10/PWM/A10, R2.Pin_0
  N10: Arduino.A5, R3.Pin_0, R4.Pin_1
  N11: CHARGER1.batt_minus_1, BATT1.negative
  N12: CHARGER1.batt_plus_1, BATT1.positive, Q1.C, R5.Pin_0
  N13: CHARGER1.dcin_plus_1, R7.Pin_1
  N14: U1.+G, R1.Pin_1
  N15: U1.+R, R2.Pin_1
  N16: U1.SW, D1.cathode, D2.cathode
  N17: Q1.B, R5.Pin_1, R6.Pin_0
  N18: Q2.B, R7.Pin_0
  N19: Q2.C, R6.Pin_1, Q3.C, D2.anode
  N20: Q3.B, R8.Pin_1

custom parts:
  Blend Micro v1.0: Blend Micro is a RedBearLab Arduino at Heart integrated development board, they have "blend"ed Arduino with Bluetooth 4.0 Low Energy (aka BLE or Bluetooth Smart) into a single board. It is targeted for makers to develop low power Internet-Of-Things (IoT) projects quickly and easily. The micro-controller unit (MCU) is Atmel ATmega32u4 and the BLE chip is Nordic nRF8001. Blend Micro runs as BLE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
  LiPoly Battery (1300mAh): Lithium Ion Polymer Battery (1300mAh)
